// Logisim project design.circ as structural Verilog: 1 circuit, main circuit main
module main (
  input  cs2,
  input  cs1,
  input  cs0,
  input  a3,
  input  a2,
  input  a1,
  input  a0,
  input  b3,
  input  b2,
  input  b1,
  input  b0,
  output C,
  output S,
  output V,
  output Z,
  output s3,
  output s2,
  output s1,
  output s0
);

  wire n7400_1__3__1y, n7400_1__6__2y, n7400_1__8__3y, n7400_1__11__4y, n7408_1__3__1y, n7408_1__6__2y,
       n7408_1__8__3y, n7408_1__11__4y, n7432_1__3__1y, n7432_1__6__2y, n7432_1__8__3y, n7432_1__11__4y,
       n7483_1__2__s3, n7483_1__6__s2, n7483_1__9__s1, n7483_1__15__s4, n7486_1__6__2y, n7486_1__8__3y,
       n7486_2__3__1y, n7486_2__6__2y, n7486_2__8__3y, n7486_2__11__4y, n74138_1__7__y7, n74138_1__9__y6,
       n74138_1__10__y5, n74138_1__13__y2, n74138_1__14__y1, n74138_1__15__y0, n74157_1__4__y1,
       n74157_1__7__y2, n74157_1__9__y3, n74157_1__12__y4, n74157_3__4__y1, n74157_3__7__y2, n74157_3__9__y3,
       n74157_3__12__y4;

  // Probe on n7400_1__3__1y
  // Probe on n7400_1__11__4y
  // Probe on n7432_1__6__2y
  // Probe on n74138_1__10__y5
  // Probe on n7400_1__6__2y
  _7400 u_7400_1 (
    ._1__1A(cs0), ._2__1B(cs0), ._3__1Y(n7400_1__3__1y), ._4__2A(n74138_1__10__y5),
    ._5__2B(n74138_1__14__y1), ._6__2Y(n7400_1__6__2y), ._7__GND(1'b0), ._14__Vcc(1'b1),
    ._13__4B(n74138_1__9__y6), ._12__4A(n74138_1__7__y7), ._11__4Y(n7400_1__11__4y),
    ._10__3B(n74138_1__15__y0), ._9__3A(n74138_1__13__y2), ._8__3Y(n7400_1__8__3y));
  _7432 u_7432_1 (
    ._1__1A(S), ._2__1B(s2), ._3__1Y(n7432_1__3__1y), ._4__2A(n7400_1__11__4y), ._5__2B(n7400_1__8__3y),
    ._6__2Y(n7432_1__6__2y), ._7__GND(1'b0), ._14__Vcc(1'b1), ._13__4B(s0), ._12__4A(n7432_1__8__3y),
    ._11__4Y(n7432_1__11__4y), ._10__3B(s1), ._9__3A(n7432_1__3__1y), ._8__3Y(n7432_1__8__3y));
  _74138 u_74138_1 (
    ._1__A(cs0), ._2__B(cs1), ._3__C(cs2), ._4__G2A(1'b0), ._5__G2B(1'b0), ._6__G1(1'b1),
    ._7__Y7(n74138_1__7__y7), ._8__GND(1'b0), ._16__Vcc(1'b1), ._15__Y0(n74138_1__15__y0),
    ._14__Y1(n74138_1__14__y1), ._13__Y2(n74138_1__13__y2), ._10__Y5(n74138_1__10__y5),
    ._9__Y6(n74138_1__9__y6));  // open: _12__Y3, _11__Y4
  _7486 u_7486_1 (
    ._1__1A(1'b1), ._2__1B(n7432_1__11__4y), ._3__1Y(Z), ._4__2A(n7483_1__15__s4), ._5__2B(C),
    ._6__2Y(n7486_1__6__2y), ._7__GND(1'b0), ._14__Vcc(1'b1), ._13__4B(n74157_3__9__y3),
    ._12__4A(n7486_1__8__3y), ._11__4Y(V), ._10__3B(a3), ._9__3A(n7486_1__6__2y), ._8__3Y(n7486_1__8__3y));
  _7408 u_7408_1 (
    ._1__1A(b0), ._2__1B(a0), ._3__1Y(n7408_1__3__1y), ._4__2A(b1), ._5__2B(a1), ._6__2Y(n7408_1__6__2y),
    ._7__GND(1'b0), ._14__Vcc(1'b1), ._13__4B(b2), ._12__4A(a2), ._11__4Y(n7408_1__11__4y), ._10__3B(a3),
    ._9__3A(b3), ._8__3Y(n7408_1__8__3y));
  _74157 u_74157_1 (
    ._1__S(n74138_1__10__y5), ._2__A1(n7486_2__3__1y), ._3__B1(n7408_1__3__1y), ._4__Y1(n74157_1__4__y1),
    ._5__A2(n7486_2__6__2y), ._6__B2(n7408_1__6__2y), ._7__Y2(n74157_1__7__y2), ._8__GND(1'b0),
    ._16__Vcc(1'b1), ._15__G(1'b0), ._14__A4(n7486_2__11__4y), ._13__B4(n7408_1__11__4y),
    ._12__Y4(n74157_1__12__y4), ._11__A3(n7486_2__8__3y), ._10__B3(n7408_1__8__3y), ._9__Y3(n74157_1__9__y3));
  _7486 u_7486_2 (
    ._1__1A(b0), ._2__1B(a0), ._3__1Y(n7486_2__3__1y), ._4__2A(b1), ._5__2B(a1), ._6__2Y(n7486_2__6__2y),
    ._7__GND(1'b0), ._14__Vcc(1'b1), ._13__4B(b2), ._12__4A(a2), ._11__4Y(n7486_2__11__4y), ._10__3B(a3),
    ._9__3A(b3), ._8__3Y(n7486_2__8__3y));
  _74157 u_74157_2 (
    ._1__S(n7400_1__6__2y), ._2__A1(n7483_1__9__s1), ._3__B1(n74157_1__4__y1), ._4__Y1(s0),
    ._5__A2(n7483_1__6__s2), ._6__B2(n74157_1__7__y2), ._7__Y2(s1), ._8__GND(1'b0), ._16__Vcc(1'b1),
    ._15__G(1'b0), ._14__A4(n7483_1__2__s3), ._13__B4(n74157_1__12__y4), ._12__Y4(s2),
    ._11__A3(n7483_1__15__s4), ._10__B3(n74157_1__9__y3), ._9__Y3(S));
  _74157 u_74157_3 (
    ._1__S(n7432_1__6__2y), ._2__A1(n7400_1__3__1y), ._3__B1(b0), ._4__Y1(n74157_3__4__y1),
    ._5__A2(n7400_1__3__1y), ._6__B2(b1), ._7__Y2(n74157_3__7__y2), ._8__GND(1'b0), ._16__Vcc(1'b1),
    ._15__G(1'b0), ._14__A4(n7400_1__3__1y), ._13__B4(b2), ._12__Y4(n74157_3__12__y4),
    ._11__A3(n7400_1__3__1y), ._10__B3(b3), ._9__Y3(n74157_3__9__y3));
  _7483 u_7483_1 (
    ._1__A4(a3), ._2__S3(n7483_1__2__s3), ._3__A3(a2), ._4__B3(n74157_3__12__y4), ._5__Vcc(1'b1),
    ._6__S2(n7483_1__6__s2), ._7__B2(n74157_3__7__y2), ._8__A2(a1), ._16__B4(n74157_3__9__y3),
    ._15__S4(n7483_1__15__s4), ._14__Cout(C), ._13__Cin(n7400_1__11__4y), ._12__GND(1'b0),
    ._11__B1(n74157_3__4__y1), ._10__A1(a0), ._9__S1(n7483_1__9__s1));

  assign s3 = S;
endmodule
