// Logisim project ComparatorLib.circ as structural Verilog: 1 circuit, main circuit 12BitMagnitudeComparator
// 12Comp
module _12BitMagnitudeComparator (
  input  SA,
  input  SB,
  input  [11:0] A,
  input  [11:0] B,
  output Switch,
  output A_B
);

  wire ic_7485_1_p10, ic_7485_2_p12, ic_7485_2_p14, ic_7485_2_p15, ic_7485_2_p16, ic_7485_3_p12,
       n7486_1__3__1y, n7486_1__8__3y;

  _7486 u_7486_1 (
    ._1__1A(SA), ._2__1B(SB), ._3__1Y(n7486_1__3__1y), ._7__GND(1'b0), ._14__Vcc(1'b1), ._10__3B(SB),
    ._9__3A(A_B), ._8__3Y(n7486_1__8__3y));  // open: _4__2A, _5__2B, _6__2Y, _13__4B, _12__4A, _11__4Y
  // IC_7485 ic_7485_1: pin names not known; wires that end beside it: A[0], A[1], A[2], A[3], B[0], B[1], B[2], B[3], 1'b0, ic_7485_1_p10
  // IC_7485 ic_7485_2: pin names not known; wires that end beside it: 1'b1, 1'b0, A[4], A[5], A[6], A[7], B[4], B[5], B[6], B[7], ic_7485_1_p10, ic_7485_2_p12, ic_7485_2_p12, ic_7485_2_p14, ic_7485_2_p15, ic_7485_2_p16
  // IC_7485 ic_7485_3: pin names not known; wires that end beside it: ic_7485_2_p14, A[8], A[9], A[10], A[11], B[8], B[9], B[10], B[11], ic_7485_2_p15, ic_7485_2_p16, ic_7485_3_p12, ic_7485_3_p12, A_B
  _7408 u_7408_1 (
    ._1__1A(n7486_1__3__1y), ._2__1B(n7486_1__8__3y), ._3__1Y(Switch));  // open: _4__2A, _5__2B, _6__2Y, _7__GND, _14__Vcc, _13__4B, _12__4A, _11__4Y, _10__3B, _9__3A, _8__3Y
endmodule
