// Logisim project FPA.circ as structural Verilog: 2 circuits, main circuit main
module main (
  input  [31:0] A,
  input  [31:0] B,
  output [31:0] Result
);

  FPA fpa_1 (.A(A), .B(B), .Result(Result));
endmodule

module FPA (
  input  [31:0] A,
  input  [31:0] B,
  output [31:0] Result
);

  wire addedinp_1_a_b, addedinp_1_cout, addedinp_1_flag, addedinp_1_sa, addedinp_1_saxorsb, addedinp_1_sb,
       addedinp_1_sign_bit, inputcheck_1_flag, n7408_1__3__1y, normalization_1_valid,
       roundingmachine_1_exp_cin;
  wire [11:0] addedinp_1_exp_large, n12adder_1_s, normalization_1_add_with_exp;
  wire [18:0] n32to19_1_o;
  wire [31:0] addedinp_1_to_normalize, n0handler_1_o, n0handler_2_o, n32mux2x1_1_o, normalization_1_out,
       outputprocess_1_float, roundingmachine_1_o;

  _0handler u_0handler_1 (.A(A), .O(n0handler_1_o));
  _0handler u_0handler_2 (.A(B), .O(n0handler_2_o));
  InputCheck inputcheck_1 (.A(n0handler_1_o), .B(n0handler_2_o), .flag(inputcheck_1_flag));  // open: A0
  AddedInp addedinp_1 (
    .A(n0handler_1_o), .B(n0handler_2_o), .A_B(addedinp_1_a_b), .Flag(addedinp_1_flag), .SA(addedinp_1_sa),
    .SB(addedinp_1_sb), .to_normalize(addedinp_1_to_normalize), .Cout(addedinp_1_cout),
    .Sign_bit(addedinp_1_sign_bit), .Exp_Large(addedinp_1_exp_large), .SAxorSB(addedinp_1_saxorsb));
  Normalization normalization_1 (
    .SA(addedinp_1_sa), .SB(addedinp_1_sb), .I(addedinp_1_to_normalize), .Exp(addedinp_1_exp_large),
    .S1xorS2(addedinp_1_saxorsb), .Cout(addedinp_1_cout), .Valid(normalization_1_valid),
    .Out(normalization_1_out), .Add_with_exp(normalization_1_add_with_exp));
  _7408 u_7408_1 (
    ._1__1A(inputcheck_1_flag), ._2__1B(addedinp_1_flag), ._3__1Y(n7408_1__3__1y), ._7__GND(1'b0),
    ._14__Vcc(1'b1));  // open: _4__2A, _5__2B, _6__2Y, _13__4B, _12__4A, _11__4Y, _10__3B, _9__3A, _8__3Y
  RoundingMachine roundingmachine_1 (
    .A(normalization_1_out), .O(roundingmachine_1_o), .Exp_Cin(roundingmachine_1_exp_cin));
  _12Adder u_12adder_1 (
    .A(addedinp_1_exp_large), .B(normalization_1_add_with_exp), .Cin(roundingmachine_1_exp_cin),
    .S(n12adder_1_s));  // open: Cout
  _32to19 u_32to19_1 (.A(roundingmachine_1_o), .O(n32to19_1_o));
  OutputProcess outputprocess_1 (
    .Sign(addedinp_1_sign_bit), .Exp(n12adder_1_s), .Frac(n32to19_1_o), .Float(outputprocess_1_float));
  _32Mux4X1 u_32mux4x1_1 (
    .A(n0handler_2_o), .B(n0handler_1_o), .C(n32mux2x1_1_o), .D(n32mux2x1_1_o), .S1(n7408_1__3__1y),
    .S0(addedinp_1_a_b), .E_prime(1'b0), .O(Result));
  _32Mux2X1 u_32mux2x1_1 (
    .A({32{1'b0}}), .B(outputprocess_1_float), .E_prime(1'b0), .S(normalization_1_valid), .O(n32mux2x1_1_o));
endmodule
