// Logisim project NormalizerLib.circ as structural Verilog: 1 circuit, main circuit Normalization
// Normalize
module Normalization (
  input  SA,
  input  SB,
  input  [31:0] I,
  input  [11:0] Exp,
  input  Cout,
  input  S1xorS2,
  output Valid,
  output [31:0] Out,
  output [11:0] Add_with_exp
);

  wire n12is0_1_o, n7404_1__12__6y, n7432_1__3__1y, n7486_1__11__4y, shiftfinder_1_va;
  wire [4:0] shiftfinder_1_o;
  wire [11:0] n2compl12_1_o, n5to12_1_o, n5to12_2_o;
  wire [31:0] arbleftshift_1_o, n1leftshift_1_o, n32mux2x1_1_o;

  ShiftFinder shiftfinder_1 (.I(I), .Va(shiftfinder_1_va), .O(shiftfinder_1_o));
  _1LeftShift u_1leftshift_1 (.A(I), .S(1'b1), .O(n1leftshift_1_o));
  ArbLeftShift arbleftshift_1 (.A(n1leftshift_1_o), .C(shiftfinder_1_o), .O(arbleftshift_1_o));
  _32Mux2X1 u_32mux2x1_1 (.A(n1leftshift_1_o), .B(I), .E_prime(1'b0), .S(Cout), .O(n32mux2x1_1_o));
  _32Mux2X1 u_32mux2x1_2 (.A(n32mux2x1_1_o), .B(arbleftshift_1_o), .E_prime(1'b0), .S(S1xorS2), .O(Out));
  _5to12 u_5to12_1 (.A(shiftfinder_1_o), .O(n5to12_1_o));
  _7486 u_7486_1 (
    ._7__GND(1'b0), ._14__Vcc(1'b1), ._13__4B(SA), ._12__4A(SB), ._11__4Y(n7486_1__11__4y));  // open: _1__1A, _2__1B, _3__1Y, _4__2A, _5__2B, _6__2Y, _10__3B, _9__3A, _8__3Y
  _5to12 u_5to12_2 (.A({4'b0000, Cout}), .O(n5to12_2_o));
  _2Compl12 u_2compl12_1 (.A(n5to12_1_o), .O(n2compl12_1_o));
  _7404 u_7404_1 (
    ._7__GND(1'b0), ._14__Vcc(1'b1), ._13__6A(n7486_1__11__4y), ._12__6Y(n7404_1__12__6y));  // open: _1__1A, _2__1Y, _3__2A, _4__2Y, _5__3A, _6__3Y, _11__5A, _10__5Y, _9__4A, _8__4Y
  _12Mux2X1 u_12mux2x1_1 (.A(n5to12_2_o), .B(n2compl12_1_o), .E_prime(1'b0), .S(S1xorS2), .O(Add_with_exp));
  _12Is0 u_12is0_1 (.A(Exp), .O(n12is0_1_o));
  _7432 u_7432_1 (
    ._1__1A(shiftfinder_1_va), ._2__1B(n7404_1__12__6y), ._3__1Y(n7432_1__3__1y), ._7__GND(1'b0),
    ._14__Vcc(1'b1));  // open: _4__2A, _5__2B, _6__2Y, _13__4B, _12__4A, _11__4Y, _10__3B, _9__3A, _8__3Y
  _7408 u_7408_1 (
    ._7__GND(1'b0), ._14__Vcc(1'b1), ._13__4B(n7432_1__3__1y), ._12__4A(n12is0_1_o), ._11__4Y(Valid));  // open: _1__1A, _2__1B, _3__1Y, _4__2A, _5__2B, _6__2Y, _10__3B, _9__3A, _8__3Y
endmodule
