// Logisim project RoundingMachine.circ as structural Verilog: 1 circuit, main circuit RoundingMachine
// RM
module RoundingMachine (
  input  [31:0] A,
  output [31:0] O,
  output Exp_Cin
);

  wire [13:13] rounding_1_o;

  Rounding rounding_1 (.A(A), .O(rounding_1_o[13]));
  _32Adder u_32adder_1 (.A({{18{1'b0}}, rounding_1_o[13], {13{1'b0}}}), .B(A), .Cin(1'b0), .S(O), .Cout(Exp_Cin));
endmodule
