// Logisim project ShiftLib.circ as structural Verilog: 13 circuits, main circuit 1LeftShift
// 1LS
module _1LeftShift (
  input  [31:0] A,
  input  S,
  output [31:0] O
);

  _32Mux2X1 u_32mux2x1_1 (.A(A), .B({A[30:0], 1'b0}), .E_prime(1'b0), .S(S), .O(O));
endmodule

// 2LS
module _2LeftShift (
  input  [31:0] A,
  input  S,
  output [31:0] O
);

  _32Mux2X1 u_32mux2x1_1 (.A(A), .B({A[29:0], 2'b00}), .E_prime(1'b0), .S(S), .O(O));
endmodule

// 4LS
module _4LeftShift (
  input  [31:0] A,
  input  S,
  output [31:0] O
);

  _32Mux2X1 u_32mux2x1_1 (.A(A), .B({A[27:0], 4'b0000}), .E_prime(1'b0), .S(S), .O(O));
endmodule

// 8LS
module _8LeftShift (
  input  [31:0] A,
  input  S,
  output [31:0] O
);

  _32Mux2X1 u_32mux2x1_1 (.A(A), .B({A[23:0], {8{1'b0}}}), .E_prime(1'b0), .S(S), .O(O));
endmodule

// 16LS
module _16LeftShift (
  input  [31:0] A,
  input  S,
  output [31:0] O
);

  _32Mux2X1 u_32mux2x1_1 (.A(A), .B({A[15:0], {16{1'b0}}}), .E_prime(1'b0), .S(S), .O(O));
endmodule

// ALS
module ArbLeftShift (
  input  [31:0] A,
  input  [4:0] C,
  output [31:0] O
);

  wire [31:0] n1leftshift_1_o, n2leftshift_1_o, n4leftshift_1_o, n8leftshift_1_o;

  _1LeftShift u_1leftshift_1 (.A(A), .S(C[0]), .O(n1leftshift_1_o));
  _2LeftShift u_2leftshift_1 (.A(n1leftshift_1_o), .S(C[1]), .O(n2leftshift_1_o));
  _4LeftShift u_4leftshift_1 (.A(n2leftshift_1_o), .S(C[2]), .O(n4leftshift_1_o));
  _8LeftShift u_8leftshift_1 (.A(n4leftshift_1_o), .S(C[3]), .O(n8leftshift_1_o));
  _16LeftShift u_16leftshift_1 (.A(n8leftshift_1_o), .S(C[4]), .O(O));
endmodule

// 1RS
module _1RightShift (
  input  [31:0] A,
  input  S,
  output [31:0] O
);

  _32Mux2X1 u_32mux2x1_1 (.A(A), .B({1'b0, A[31:1]}), .E_prime(1'b0), .S(S), .O(O));
endmodule

// 2RS
module _2RightShift (
  input  [31:0] A,
  input  S,
  output [31:0] O
);

  _32Mux2X1 u_32mux2x1_1 (.A(A), .B({2'b00, A[31:2]}), .E_prime(1'b0), .S(S), .O(O));
endmodule

// 4RS
module _4RightShift (
  input  [31:0] A,
  input  S,
  output [31:0] O
);

  _32Mux2X1 u_32mux2x1_1 (.A(A), .B({4'b0000, A[31:4]}), .E_prime(1'b0), .S(S), .O(O));
endmodule

// 8RS
module _8RightShift (
  input  [31:0] A,
  input  S,
  output [31:0] O
);

  _32Mux2X1 u_32mux2x1_1 (.A(A), .B({{8{1'b0}}, A[31:8]}), .E_prime(1'b0), .S(S), .O(O));
endmodule

// 16RS
module _16RightShift (
  input  [31:0] A,
  input  S,
  output [31:0] O
);

  _32Mux2X1 u_32mux2x1_1 (.A(A), .B({{16{1'b0}}, A[31:16]}), .E_prime(1'b0), .S(S), .O(O));
endmodule

// ARS
module ArbRightShift (
  input  [31:0] A,
  input  [4:0] C,
  output [31:0] O
);

  wire [31:0] n1rightshift_1_o, n2rightshift_1_o, n4rightshift_1_o, n8rightshift_1_o;

  _1RightShift u_1rightshift_1 (.A(A), .S(C[0]), .O(n1rightshift_1_o));
  _2RightShift u_2rightshift_1 (.A(n1rightshift_1_o), .S(C[1]), .O(n2rightshift_1_o));
  _4RightShift u_4rightshift_1 (.A(n2rightshift_1_o), .S(C[2]), .O(n4rightshift_1_o));
  _8RightShift u_8rightshift_1 (.A(n4rightshift_1_o), .S(C[3]), .O(n8rightshift_1_o));
  _16RightShift u_16rightshift_1 (.A(n8rightshift_1_o), .S(C[4]), .O(O));
endmodule

// RSWE
module RigthShiftWithEmpty (
  input  [31:0] A,
  input  [11:0] in_2,
  output [31:0] O
);

  wire n32mux2x1_1_p4, n7432_1__3__1y, n7432_1__6__2y, n7432_2__3__1y, n7432_2__6__2y, n7432_2__8__3y,
       n7432_2__11__4y;
  wire [31:0] arbrightshift_1_o;

  _7432 u_7432_1 (
    ._1__1A(n7432_1__6__2y), ._2__1B(in_2[11]), ._3__1Y(n7432_1__3__1y), ._4__2A(in_2[10]),
    ._5__2B(n7432_2__3__1y), ._6__2Y(n7432_1__6__2y), ._7__GND(1'b0), ._14__Vcc(1'b1));  // open: _13__4B, _12__4A, _11__4Y, _10__3B, _9__3A, _8__3Y
  _7432 u_7432_2 (
    ._1__1A(in_2[9]), ._2__1B(n7432_2__6__2y), ._3__1Y(n7432_2__3__1y), ._4__2A(in_2[8]),
    ._5__2B(n7432_2__11__4y), ._6__2Y(n7432_2__6__2y), ._7__GND(1'b0), ._14__Vcc(1'b1), ._13__4B(in_2[7]),
    ._12__4A(n7432_2__8__3y), ._11__4Y(n7432_2__11__4y), ._10__3B(in_2[6]), ._9__3A(in_2[5]),
    ._8__3Y(n7432_2__8__3y));
  ArbRightShift arbrightshift_1 (.A(A), .C(in_2[4:0]), .O(arbrightshift_1_o));
  // _32Mux2X1 32mux2x1_1: pin names not known; wires that end beside it: arbrightshift_1_o, {32{1'b0}}, 1'b0, n32mux2x1_1_p4, n7432_1__3__1y, O, n32mux2x1_1_p4
endmodule
