// Logisim project Added.circ as structural Verilog: 2 circuits, main circuit AddedInp
// AddInp
module AddedInp (
  input  [31:0] A,
  input  [31:0] B,
  output [31:0] to_normalize,
  output Cout,
  output Sign_bit,
  output [11:0] Exp_Large,
  output SAxorSB
);

  wire inputhandle_1_switch, n7408_1__11__4y, n7486_1__11__4y, n74157_1__4__y1;
  wire [11:0] inputhandle_1_expdiff;
  wire [31:0] inputhandle_1_large, inputhandle_1_small, n2compl32_1_o, n2compl32_2_o, n32adder_1_s,
       n32mux2x1_1_o, rigthshiftwithempty_1_o;

  InputHandle inputhandle_1 (
    .SA(A[31]), .SB(B[31]), .A_Frac(A[18:0]), .B_Frac(B[18:0]), .A_Exp(A[30:19]), .B_Exp(B[30:19]),
    .Switch(inputhandle_1_switch), .Large(inputhandle_1_large), .Small(inputhandle_1_small),
    .ExpDiff(inputhandle_1_expdiff), .Exp_Large(Exp_Large));
  _7486 u_7486_1 (
    ._1__1A(B[31]), ._2__1B(A[31]), ._3__1Y(SAxorSB), ._4__2A(inputhandle_1_switch),
    ._5__2B(n74157_1__4__y1), ._6__2Y(Sign_bit), ._7__GND(1'b0), ._14__Vcc(1'b1), ._13__4B(1'b1),
    ._12__4A(Cout), ._11__4Y(n7486_1__11__4y));  // open: _10__3B, _9__3A, _8__3Y
  _7408 u_7408_1 (
    ._7__GND(1'b0), ._14__Vcc(1'b1), ._13__4B(SAxorSB), ._12__4A(n7486_1__11__4y), ._11__4Y(n7408_1__11__4y));  // open: _1__1A, _2__1B, _3__1Y, _4__2A, _5__2B, _6__2Y, _10__3B, _9__3A, _8__3Y
  RigthShiftWithEmpty rigthshiftwithempty_1 (
    .A(inputhandle_1_small), .in_2(inputhandle_1_expdiff), .O(rigthshiftwithempty_1_o));
  _2Compl32 u_2compl32_1 (.A(rigthshiftwithempty_1_o), .O(n2compl32_1_o));
  _32Mux2X1 u_32mux2x1_1 (
    .A(rigthshiftwithempty_1_o), .B(n2compl32_1_o), .E_prime(1'b0), .S(SAxorSB), .O(n32mux2x1_1_o));
  _32Adder u_32adder_1 (.A(inputhandle_1_large), .B(n32mux2x1_1_o), .Cin(1'b0), .S(n32adder_1_s), .Cout(Cout));
  _2Compl32 u_2compl32_2 (.A(n32adder_1_s), .O(n2compl32_2_o));
  _32Mux2X1 u_32mux2x1_2 (.A(n32adder_1_s), .B(n2compl32_2_o), .E_prime(1'b0), .S(n7408_1__11__4y), .O(to_normalize));
  _74157 u_74157_1 (
    ._1__S(SAxorSB), ._2__A1(A[31]), ._3__B1(n7486_1__11__4y), ._4__Y1(n74157_1__4__y1), ._15__G(1'b0));  // open: _5__A2, _6__B2, _7__Y2, _8__GND, _16__Vcc, _14__A4, _13__B4, _12__Y4, _11__A3, _10__B3, _9__Y3
endmodule

module test (
  input  [31:0] A,
  input  [31:0] B,
  output [31:0] t0_normalize,
  output Cout,
  output Sign_bit,
  output [11:0] Exp_Large,
  output S1xorS2
);

  AddedInp addedinp_1 (
    .A(A), .B(B), .to_normalize(t0_normalize), .Cout(Cout), .Sign_bit(Sign_bit), .Exp_Large(Exp_Large),
    .SAxorSB(S1xorS2));
endmodule
