// Logisim project AdderLib.circ as structural Verilog: 9 circuits, main circuit 4Adder
// 4Add
module _4Adder (
  input  [3:0] A,
  input  [3:0] B,
  input  Cin,
  output [3:0] S,
  output Cout
);

  _7483 u_7483_1 (
    ._1__A4(A[3]), ._2__S3(S[2]), ._3__A3(A[2]), ._4__B3(B[2]), ._5__Vcc(1'b1), ._6__S2(S[1]), ._7__B2(B[1]),
    ._8__A2(A[1]), ._16__B4(B[3]), ._15__S4(S[3]), ._14__Cout(Cout), ._13__Cin(Cin), ._12__GND(1'b0),
    ._11__B1(B[0]), ._10__A1(A[0]), ._9__S1(S[0]));
endmodule

// 32Add
module _32Adder (
  input  [31:0] A,
  input  [31:0] B,
  input  Cin,
  output [31:0] S,
  output Cout
);

  wire n4adder_1_cout, n4adder_2_cout, n4adder_3_cout, n4adder_4_cout, n4adder_5_cout, n4adder_6_cout,
       n4adder_7_cout;

  _4Adder u_4adder_1 (.A(A[3:0]), .B(B[3:0]), .Cin(Cin), .S(S[3:0]), .Cout(n4adder_1_cout));
  _4Adder u_4adder_2 (.A(A[7:4]), .B(B[7:4]), .Cin(n4adder_1_cout), .S(S[7:4]), .Cout(n4adder_2_cout));
  _4Adder u_4adder_3 (.A(A[11:8]), .B(B[11:8]), .Cin(n4adder_2_cout), .S(S[11:8]), .Cout(n4adder_3_cout));
  _4Adder u_4adder_4 (.A(A[15:12]), .B(B[15:12]), .Cin(n4adder_3_cout), .S(S[15:12]), .Cout(n4adder_4_cout));
  _4Adder u_4adder_5 (.A(A[19:16]), .B(B[19:16]), .Cin(n4adder_4_cout), .S(S[19:16]), .Cout(n4adder_5_cout));
  _4Adder u_4adder_6 (.A(A[23:20]), .B(B[23:20]), .Cin(n4adder_5_cout), .S(S[23:20]), .Cout(n4adder_6_cout));
  _4Adder u_4adder_7 (.A(A[27:24]), .B(B[27:24]), .Cin(n4adder_6_cout), .S(S[27:24]), .Cout(n4adder_7_cout));
  _4Adder u_4adder_8 (.A(A[31:28]), .B(B[31:28]), .Cin(n4adder_7_cout), .S(S[31:28]), .Cout(Cout));
endmodule

// 12Add
module _12Adder (
  input  [11:0] A,
  input  [11:0] B,
  input  Cin,
  output [11:0] S,
  output Cout
);

  wire n4adder_1_cout, n4adder_2_cout;

  _4Adder u_4adder_1 (.A(A[3:0]), .B(B[3:0]), .Cin(Cin), .S(S[3:0]), .Cout(n4adder_1_cout));
  _4Adder u_4adder_2 (.A(A[7:4]), .B(B[7:4]), .Cin(n4adder_1_cout), .S(S[7:4]), .Cout(n4adder_2_cout));
  _4Adder u_4adder_3 (.A(A[11:8]), .B(B[11:8]), .Cin(n4adder_2_cout), .S(S[11:8]), .Cout(Cout));
endmodule

// 1Cl4
module _1Compl4 (
  input  [3:0] A,
  output [3:0] O
);

  _7486 u_7486_1 (
    ._1__1A(A[0]), ._2__1B(1'b1), ._3__1Y(O[0]), ._4__2A(A[1]), ._5__2B(1'b1), ._6__2Y(O[1]), ._7__GND(1'b0),
    ._14__Vcc(1'b1), ._13__4B(1'b1), ._12__4A(A[3]), ._11__4Y(O[3]), ._10__3B(1'b1), ._9__3A(A[2]),
    ._8__3Y(O[2]));
endmodule

// 1Cl12
module _1Compl12 (
  input  [11:0] A,
  output [11:0] O
);

  _1Compl4 u_1compl4_1 (.A(A[3:0]), .O(O[3:0]));
  _1Compl4 u_1compl4_2 (.A(A[7:4]), .O(O[7:4]));
  _1Compl4 u_1compl4_3 (.A(A[11:8]), .O(O[11:8]));
endmodule

// 1Cl32
module _1Compl32 (
  input  [31:0] A,
  output [31:0] O
);

  _1Compl4 u_1compl4_1 (.A(A[3:0]), .O(O[3:0]));
  _1Compl4 u_1compl4_2 (.A(A[7:4]), .O(O[7:4]));
  _1Compl4 u_1compl4_3 (.A(A[11:8]), .O(O[11:8]));
  _1Compl4 u_1compl4_4 (.A(A[15:12]), .O(O[15:12]));
  _1Compl4 u_1compl4_5 (.A(A[19:16]), .O(O[19:16]));
  _1Compl4 u_1compl4_6 (.A(A[23:20]), .O(O[23:20]));
  _1Compl4 u_1compl4_7 (.A(A[27:24]), .O(O[27:24]));
  _1Compl4 u_1compl4_8 (.A(A[31:28]), .O(O[31:28]));
endmodule

// 2Cl12
module _2Compl12 (
  input  [11:0] A,
  output [11:0] O
);

  wire [11:0] n1compl12_1_o;

  _1Compl12 u_1compl12_1 (.A(A), .O(n1compl12_1_o));
  _12Adder u_12adder_1 (.A(n1compl12_1_o), .B({12{1'b0}}), .Cin(1'b1), .S(O));  // open: Cout
endmodule

// 2Cl32
module _2Compl32 (
  input  [31:0] A,
  output [31:0] O
);

  wire [31:0] n1compl32_1_o;

  _1Compl32 u_1compl32_1 (.A(A), .O(n1compl32_1_o));
  _32Adder u_32adder_1 (.A(n1compl32_1_o), .B({32{1'b0}}), .Cin(1'b1), .S(O));  // open: Cout
endmodule

module _12Sub (
  input  [11:0] A,
  input  [11:0] B,
  output [11:0] A_B
);

  wire [11:0] n1compl12_1_o;

  _1Compl12 u_1compl12_1 (.A(B), .O(n1compl12_1_o));
  _12Adder u_12adder_1 (.A(A), .B(n1compl12_1_o), .Cin(1'b1), .S(A_B));  // open: Cout
endmodule
