// Logisim project EncoderLib.circ as structural Verilog: 3 circuits, main circuit 8x3 Priority Encoder
// 8X3PE
module _8x3_Priority_Encoder (
  input  I7,
  input  I6,
  input  I5,
  input  I4,
  input  I3,
  input  I2,
  input  I1,
  input  I0,
  output O2,
  output O1,
  output O0,
  output Va
);

  wire n7432_1__3__1y, n7432_1__6__2y, n7432_1__8__3y, n7432_1__11__4y, n7432_2__3__1y, n7432_2__6__2y;

  _7432 u_7432_1 (
    ._1__1A(I7), ._2__1B(I6), ._3__1Y(n7432_1__3__1y), ._4__2A(n7432_1__3__1y), ._5__2B(I5),
    ._6__2Y(n7432_1__6__2y), ._7__GND(1'b0), ._14__Vcc(1'b1), ._13__4B(n7432_1__8__3y), ._12__4A(I3),
    ._11__4Y(n7432_1__11__4y), ._10__3B(I4), ._9__3A(n7432_1__6__2y), ._8__3Y(n7432_1__8__3y));
  _7432 u_7432_2 (
    ._1__1A(n7432_1__11__4y), ._2__1B(I2), ._3__1Y(n7432_2__3__1y), ._4__2A(n7432_2__3__1y), ._5__2B(I1),
    ._6__2Y(n7432_2__6__2y), ._7__GND(1'b0), ._14__Vcc(1'b1), ._13__4B(n7432_2__6__2y), ._12__4A(I0),
    ._11__4Y(Va));  // open: _10__3B, _9__3A, _8__3Y
  _74147 u_74147_1 (
    ._1__I4(I3), ._2__I5(I4), ._3__I6(I5), ._4__I7(I6), ._5__I8(I7), ._6__A2(O2), ._7__A1(O1),
    ._8__GND(1'b0), ._16__Vcc(1'b1), ._13__I3(I2), ._12__I2(I1), ._11__I1(I0), ._10__I9(1'b0), ._9__A0(O0));  // open: _15__NC, _14__A3
endmodule

// Shifter
module ShiftFinder (
  input  [31:0] I,
  output Va,
  output [4:0] O
);

  wire n4x2_priority_encoder_1_o0, n4x2_priority_encoder_1_o1, n7432_1__3__1y, n7432_1__6__2y, PE0_va,
       PE1_va, PE2_va, PE3_va;
  wire [2:0] PE0_o0, PE1_o0, PE2_o0, PE3_o0;
  wire [3:0] n4mux4x1_1_o;

  _7432 u_7432_1 (
    ._1__1A(PE0_va), ._2__1B(PE1_va), ._3__1Y(n7432_1__3__1y), ._4__2A(n7432_1__3__1y), ._5__2B(PE2_va),
    ._6__2Y(n7432_1__6__2y), ._7__GND(1'b0), ._14__Vcc(1'b1), ._10__3B(PE3_va), ._9__3A(n7432_1__6__2y),
    ._8__3Y(Va));  // open: _13__4B, _12__4A, _11__4Y
  _8x3_Priority_Encoder PE0 (
    .I7(I[7]), .I6(I[6]), .I5(I[5]), .I4(I[4]), .I3(I[3]), .I2(I[2]), .I1(I[1]), .I0(I[0]), .O2(PE0_o0[2]),
    .O1(PE0_o0[1]), .O0(PE0_o0[0]), .Va(PE0_va));
  _8x3_Priority_Encoder PE1 (
    .I7(I[15]), .I6(I[14]), .I5(I[13]), .I4(I[12]), .I3(I[11]), .I2(I[10]), .I1(I[9]), .I0(I[8]),
    .O2(PE1_o0[2]), .O1(PE1_o0[1]), .O0(PE1_o0[0]), .Va(PE1_va));
  _8x3_Priority_Encoder PE2 (
    .I7(I[23]), .I6(I[22]), .I5(I[21]), .I4(I[20]), .I3(I[19]), .I2(I[18]), .I1(I[17]), .I0(I[16]),
    .O2(PE2_o0[2]), .O1(PE2_o0[1]), .O0(PE2_o0[0]), .Va(PE2_va));
  _8x3_Priority_Encoder PE3 (
    .I7(I[31]), .I6(I[30]), .I5(I[29]), .I4(I[28]), .I3(I[27]), .I2(I[26]), .I1(I[25]), .I0(I[24]),
    .O2(PE3_o0[2]), .O1(PE3_o0[1]), .O0(PE3_o0[0]), .Va(PE3_va));
  _4x2_Priority_Encoder u_4x2_priority_encoder_1 (
    .I3(PE3_va), .I2(PE2_va), .I1(PE1_va), .I0(PE0_va), .O1(n4x2_priority_encoder_1_o1),
    .O0(n4x2_priority_encoder_1_o0));  // open: Va
  _4Mux4X1 u_4mux4x1_1 (
    .A({1'b0, PE0_o0}), .B({1'b0, PE1_o0}), .C({1'b0, PE2_o0}), .D({1'b0, PE3_o0}), .E_prime(1'b0),
    .S1(n4x2_priority_encoder_1_o1), .S0(n4x2_priority_encoder_1_o0), .O(n4mux4x1_1_o));
  _7404 u_7404_1 (
    ._1__1A(n4mux4x1_1_o[0]), ._2__1Y(O[0]), ._3__2A(n4mux4x1_1_o[1]), ._4__2Y(O[1]),
    ._5__3A(n4mux4x1_1_o[2]), ._6__3Y(O[2]), ._7__GND(1'b0), ._14__Vcc(1'b1),
    ._13__6A(n4x2_priority_encoder_1_o1), ._12__6Y(O[4]), ._11__5A(n4x2_priority_encoder_1_o0), ._10__5Y(O[3]));  // open: _9__4A, _8__4Y
endmodule

// 4X2PE
module _4x2_Priority_Encoder (
  input  I3,
  input  I2,
  input  I1,
  input  I0,
  output O1,
  output O0,
  output Va
);

  _8x3_Priority_Encoder u_8x3_priority_encoder_1 (
    .I7(1'b0), .I6(1'b0), .I5(1'b0), .I4(1'b0), .I3(I3), .I2(I2), .I1(I1), .I0(I0), .O1(O1), .O0(O0), .Va(Va));  // open: O2
endmodule
