// Logisim project FPA.circ as structural Verilog: 2 circuits, main circuit main
module main (
  input  [31:0] A,
  input  [31:0] B,
  output [31:0] Result
);

  FPA fpa_1 (.A(A), .B(B), .Result(Result));
endmodule

module FPA (
  input  [31:0] A,
  input  [31:0] B,
  output [31:0] Result
);

  wire addedinp_1_cout, addedinp_1_saxorsb, addedinp_1_sign_bit, normalization_1_valid,
       roundingmachine_1_exp_cin;
  wire [11:0] addedinp_1_exp_large, n12adder_1_s, normalization_1_add_with_exp;
  wire [18:0] n32to19_1_o;
  wire [31:0] addedinp_1_to_normalize, normalization_1_out, outputprocess_1_float, roundingmachine_1_o;

  AddedInp addedinp_1 (
    .A(A), .B(B), .to_normalize(addedinp_1_to_normalize), .Cout(addedinp_1_cout),
    .Sign_bit(addedinp_1_sign_bit), .Exp_Large(addedinp_1_exp_large), .SAxorSB(addedinp_1_saxorsb));
  Normalization normalization_1 (
    .I(addedinp_1_to_normalize), .S1xorS2(addedinp_1_saxorsb), .Cout(addedinp_1_cout),
    .Valid(normalization_1_valid), .Out(normalization_1_out), .Add_with_exp(normalization_1_add_with_exp));
  RoundingMachine roundingmachine_1 (
    .A(normalization_1_out), .O(roundingmachine_1_o), .Exp_Cin(roundingmachine_1_exp_cin));
  _12Adder u_12adder_1 (
    .A(addedinp_1_exp_large), .B(normalization_1_add_with_exp), .Cin(roundingmachine_1_exp_cin),
    .S(n12adder_1_s));  // open: Cout
  _32to19 u_32to19_1 (.A(roundingmachine_1_o), .O(n32to19_1_o));
  OutputProcess outputprocess_1 (
    .Sign(addedinp_1_sign_bit), .Exp(n12adder_1_s), .Frac(n32to19_1_o), .Float(outputprocess_1_float));
  _32Mux2X1 u_32mux2x1_1 (
    .A({32{1'b0}}), .B(outputprocess_1_float), .E_prime(1'b0), .S(normalization_1_valid), .O(Result));
endmodule
