// Logisim project InputHandler.circ as structural Verilog: 2 circuits, main circuit ExpDiff12
// ExpDiff
module ExpDiff12 (
  input  SA,
  input  SB,
  input  [11:0] A,
  input  [11:0] B,
  output Switch,
  output A_B,
  output [11:0] A_nB,
  output [11:0] Exp_Large
);

  wire [11:0] n12mux2x1_1_o;

  _12BitMagnitudeComparator u_12bitmagnitudecomparator_1 (.SA(SA), .SB(SB), .A(A), .B(B), .Switch(Switch), .A_B(A_B));
  _12Mux2X1 u_12mux2x1_1 (.A(A), .B(B), .E_prime(1'b0), .S(A_B), .O(n12mux2x1_1_o));
  _12Mux2X1 u_12mux2x1_2 (.A(B), .B(A), .E_prime(1'b0), .S(A_B), .O(Exp_Large));
  _12Sub u_12sub_1 (.A(Exp_Large), .B(n12mux2x1_1_o), .A_B(A_nB));
endmodule

// InpProc
module InputHandle (
  input  SA,
  input  SB,
  input  [18:0] A_Frac,
  input  [18:0] B_Frac,
  input  [11:0] A_Exp,
  input  [11:0] B_Exp,
  output Switch,
  output [31:0] Large,
  output [31:0] Small,
  output [11:0] ExpDiff,
  output [11:0] Exp_Large
);

  wire expdiff12_1_a_b;
  wire [31:0] n19to32_1_out_2, n19to32_2_out_2;

  _19to32 u_19to32_1 (.in_1(A_Frac), .out_2(n19to32_1_out_2));
  _19to32 u_19to32_2 (.in_1(B_Frac), .out_2(n19to32_2_out_2));
  ExpDiff12 expdiff12_1 (
    .SA(SA), .SB(SB), .A(A_Exp), .B(B_Exp), .Switch(Switch), .A_B(expdiff12_1_a_b), .A_nB(ExpDiff),
    .Exp_Large(Exp_Large));
  _32Mux2X1 u_32mux2x1_1 (.A(n19to32_2_out_2), .B(n19to32_1_out_2), .E_prime(1'b0), .S(expdiff12_1_a_b), .O(Large));
  _32Mux2X1 u_32mux2x1_2 (.A(n19to32_1_out_2), .B(n19to32_2_out_2), .E_prime(1'b0), .S(expdiff12_1_a_b), .O(Small));
endmodule
