// Logisim project MiscLib.circ as structural Verilog: 6 circuits, main circuit 20to32
// 20T32
module _20to32 (
  input  [19:0] in_1,
  output [31:0] out_2
);


  assign out_2 = {1'b1, in_1, {11{1'b0}}};
endmodule

// 19T32
module _19to32 (
  input  [18:0] in_1,
  output [31:0] out_2
);


  assign out_2 = {1'b1, in_1, {12{1'b0}}};
endmodule

// Rnd
module Rounding (
  input  [31:0] A,
  output O
);

  wire n7432_1__3__1y, n7432_1__6__2y, n7432_1__8__3y, n7432_1__11__4y, n7432_2__3__1y, n7432_2__6__2y,
       n7432_2__8__3y, n7432_2__11__4y, n7432_3__3__1y, n7432_3__6__2y, n7432_3__8__3y, n7432_3__11__4y;

  _7432 u_7432_1 (
    ._1__1A(A[0]), ._2__1B(A[1]), ._3__1Y(n7432_1__3__1y), ._4__2A(n7432_1__3__1y), ._5__2B(A[2]),
    ._6__2Y(n7432_1__6__2y), ._7__GND(1'b0), ._14__Vcc(1'b1), ._13__4B(n7432_1__6__2y), ._12__4A(A[3]),
    ._11__4Y(n7432_1__11__4y), ._10__3B(n7432_1__11__4y), ._9__3A(A[4]), ._8__3Y(n7432_1__8__3y));
  _7432 u_7432_2 (
    ._1__1A(n7432_1__8__3y), ._2__1B(A[5]), ._3__1Y(n7432_2__3__1y), ._4__2A(n7432_2__3__1y), ._5__2B(A[6]),
    ._6__2Y(n7432_2__6__2y), ._7__GND(1'b0), ._14__Vcc(1'b1), ._13__4B(n7432_2__6__2y), ._12__4A(A[7]),
    ._11__4Y(n7432_2__11__4y), ._10__3B(n7432_2__11__4y), ._9__3A(A[8]), ._8__3Y(n7432_2__8__3y));
  _7432 u_7432_3 (
    ._1__1A(n7432_2__8__3y), ._2__1B(A[9]), ._3__1Y(n7432_3__3__1y), ._4__2A(n7432_3__3__1y), ._5__2B(A[10]),
    ._6__2Y(n7432_3__6__2y), ._7__GND(1'b0), ._14__Vcc(1'b1), ._13__4B(n7432_3__6__2y), ._12__4A(A[11]),
    ._11__4Y(n7432_3__11__4y), ._10__3B(n7432_3__11__4y), ._9__3A(A[13]), ._8__3Y(n7432_3__8__3y));
  _7408 u_7408_1 (
    ._1__1A(n7432_3__8__3y), ._2__1B(A[12]), ._3__1Y(O), ._7__GND(1'b0), ._14__Vcc(1'b1));  // open: _4__2A, _5__2B, _6__2Y, _13__4B, _12__4A, _11__4Y, _10__3B, _9__3A, _8__3Y
endmodule

// 5T12
module _5to12 (
  input  [4:0] A,
  output [11:0] O
);


  assign O = {{7{1'b0}}, A};
endmodule

// 32T19
module _32to19 (
  input  [31:0] A,
  output [18:0] O
);


  assign O = A[31:13];
endmodule

// OP
module OutputProcess (
  input  Sign,
  input  [11:0] Exp,
  input  [18:0] Frac,
  output [31:0] Float
);


  assign Float = {Sign, Exp, Frac};
endmodule
