// Logisim project NormalizerLib.circ as structural Verilog: 1 circuit, main circuit Normalization
// Normalize
module Normalization (
  input  [31:0] I,
  input  S1xorS2,
  input  Cout,
  output Valid,
  output [31:0] Out,
  output [11:0] Add_with_exp
);

  wire [4:0] shiftfinder_1_o;
  wire [11:0] n2compl12_1_o, n5to12_1_o, n5to12_2_o;
  wire [31:0] arbleftshift_1_o, n1leftshift_1_o, n32mux2x1_1_o;

  ShiftFinder shiftfinder_1 (.I(I), .Va(Valid), .O(shiftfinder_1_o));
  _1LeftShift u_1leftshift_1 (.A(I), .S(1'b1), .O(n1leftshift_1_o));
  ArbLeftShift arbleftshift_1 (.A(n1leftshift_1_o), .C(shiftfinder_1_o), .O(arbleftshift_1_o));
  _32Mux2X1 u_32mux2x1_1 (.A(n1leftshift_1_o), .B(I), .E_prime(1'b0), .S(Cout), .O(n32mux2x1_1_o));
  _32Mux2X1 u_32mux2x1_2 (.A(n32mux2x1_1_o), .B(arbleftshift_1_o), .E_prime(1'b0), .S(S1xorS2), .O(Out));
  _5to12 u_5to12_1 (.A(shiftfinder_1_o), .O(n5to12_1_o));
  _5to12 u_5to12_2 (.A({4'b0000, Cout}), .O(n5to12_2_o));
  _2Compl12 u_2compl12_1 (.A(n5to12_1_o), .O(n2compl12_1_o));
  _12Mux2X1 u_12mux2x1_1 (.A(n5to12_2_o), .B(n2compl12_1_o), .E_prime(1'b0), .S(S1xorS2), .O(Add_with_exp));
endmodule
