// Logisim project ALU.circ as structural Verilog: 11 circuits, main circuit 4OR
module _4OR (
  input  [3:0] A,
  input  [3:0] B,
  output [3:0] O
);

  _7432 u_7432_1 (
    ._1__1A(A[3]), ._2__1B(B[3]), ._3__1Y(O[3]), ._4__2A(A[2]), ._5__2B(B[2]), ._6__2Y(O[2]), ._13__4B(A[1]),
    ._12__4A(B[1]), ._11__4Y(O[1]), ._10__3B(A[0]), ._9__3A(B[0]), ._8__3Y(O[0]));  // open: _7__GND, _14__Vcc
endmodule

module _4AND (
  input  [3:0] A,
  input  [3:0] B,
  output [3:0] O
);

  _7408 u_7408_1 (
    ._1__1A(A[3]), ._2__1B(B[3]), ._3__1Y(O[3]), ._4__2A(A[2]), ._5__2B(B[2]), ._6__2Y(O[2]), ._13__4B(A[1]),
    ._12__4A(B[1]), ._11__4Y(O[1]), ._10__3B(A[0]), ._9__3A(B[0]), ._8__3Y(O[0]));  // open: _7__GND, _14__Vcc
endmodule

module _4NOR (
  input  [3:0] A,
  input  [3:0] B,
  output [3:0] O
);

  _7402 u_7402_1 (
    ._1__1Y(O[3]), ._2__1A(A[3]), ._3__1B(B[3]), ._4__2Y(O[2]), ._5__2A(A[2]), ._6__2B(B[2]), ._13__4Y(O[1]),
    ._12__4B(A[1]), ._11__4A(B[1]), ._10__3Y(O[0]), ._9__3B(A[0]), ._8__3A(B[0]));  // open: _7__GND, _14__Vcc
endmodule

module ADD (
  input  [7:0] A,
  input  [7:0] B,
  output [7:0] O
);

  Adder adder_1 (.a(A), .b(B), .out(O), .cin(1'b0));  // open: cout
endmodule

module SUB (
  input  [7:0] A,
  input  [7:0] B,
  output [7:0] O
);

  Subtractor subtractor_1 (.a(A), .b(B), .out(O), .bin(1'b0));  // open: bout
endmodule

module SRL (
  input  [7:0] A,
  input  [7:0] Shamt,
  output [7:0] O
);

  wire [7:0] shifter_1_out;

  Shifter #(.shift("lr")) shifter_1 (.in(A), .\dist (Shamt[2:0]), .out(shifter_1_out));
  _8Mux2X1 u_8mux2x1_1 (.E_prime(1'b0), .A(shifter_1_out), .B({8{1'b0}}), .S(Shamt[3]), .out_5(O));
endmodule

module SLL (
  input  [7:0] A,
  input  [7:0] Shamt,
  output [7:0] O
);

  wire [7:0] shifter_1_out;

  Shifter shifter_1 (.in(A), .\dist (Shamt[2:0]), .out(shifter_1_out));
  _8Mux2X1 u_8mux2x1_1 (.E_prime(1'b0), .A(shifter_1_out), .B({8{1'b0}}), .S(Shamt[3]), .out_5(O));
endmodule

module ALU (
  input  [7:0] A,
  input  [7:0] B,
  input  [2:0] ALUOP,
  output [7:0] O
);

  wire [7:0] add_1_o, n8and_1_o, n8nor_1_o, n8or_1_o, sll_1_o, srl_1_o, sub_1_o;

  ADD add_1 (.A(A), .B(B), .O(add_1_o));
  SUB sub_1 (.A(A), .B(B), .O(sub_1_o));
  _8OR u_8or_1 (.A(A), .B(B), .O(n8or_1_o));
  _8AND u_8and_1 (.A(A), .B(B), .O(n8and_1_o));
  SLL sll_1 (.A(A), .Shamt(B), .O(sll_1_o));
  SRL srl_1 (.A(A), .Shamt(B), .O(srl_1_o));
  _8NOR u_8nor_1 (.A(A), .B(B), .O(n8nor_1_o));
  Multiplexer #(.select(3), .width(8)) multiplexer_1 (
    .in0(add_1_o), .in1(sub_1_o), .in2(n8or_1_o), .in3(n8and_1_o), .in4(sll_1_o), .in5(srl_1_o),
    .in6(n8nor_1_o), .out(O), .sel(ALUOP), .en(1'b1));  // open: in7
endmodule

module _8OR (
  input  [7:0] A,
  input  [7:0] B,
  output [7:0] O
);

  _4OR u_4or_1 (.A(A[3:0]), .B(B[3:0]), .O(O[3:0]));
  _4OR u_4or_2 (.A(A[7:4]), .B(B[7:4]), .O(O[7:4]));
endmodule

module _8AND (
  input  [7:0] A,
  input  [7:0] B,
  output [7:0] O
);

  _4AND u_4and_1 (.A(A[3:0]), .B(B[3:0]), .O(O[3:0]));
  _4AND u_4and_2 (.A(A[7:4]), .B(B[7:4]), .O(O[7:4]));
endmodule

module _8NOR (
  input  [7:0] A,
  input  [7:0] B,
  output [7:0] O
);

  _4NOR u_4nor_1 (.A(A[3:0]), .B(B[3:0]), .O(O[3:0]));
  _4NOR u_4nor_2 (.A(A[7:4]), .B(B[7:4]), .O(O[7:4]));
endmodule
