// Logisim project Adder.circ as structural Verilog: 2 circuits, main circuit Adder8
module Adder8 (
  input  [7:0] A,
  input  [7:0] B,
  input  Cin,
  output [7:0] S,
  output Cout
);

  wire n7483_1__14__cout;

  _7483 u_7483_1 (
    ._1__A4(A[3]), ._2__S3(S[2]), ._3__A3(A[2]), ._4__B3(B[2]), ._5__Vcc(1'b1), ._6__S2(S[1]), ._7__B2(B[1]),
    ._8__A2(A[1]), ._16__B4(B[3]), ._15__S4(S[3]), ._14__Cout(n7483_1__14__cout), ._13__Cin(Cin),
    ._12__GND(1'b0), ._11__B1(B[0]), ._10__A1(A[0]), ._9__S1(S[0]));
  _7483 u_7483_2 (
    ._1__A4(A[7]), ._2__S3(S[6]), ._3__A3(A[6]), ._4__B3(B[6]), ._5__Vcc(1'b1), ._6__S2(S[5]), ._7__B2(B[5]),
    ._8__A2(A[5]), ._16__B4(B[7]), ._15__S4(S[7]), ._14__Cout(Cout), ._13__Cin(n7483_1__14__cout),
    ._12__GND(1'b0), ._11__B1(B[4]), ._10__A1(A[4]), ._9__S1(S[4]));
endmodule

module Adder4 (
  input  [3:0] A,
  input  [3:0] B,
  input  Cin,
  output [3:0] S,
  output Cout
);

  _7483 u_7483_1 (
    ._1__A4(A[3]), ._2__S3(S[2]), ._3__A3(A[2]), ._4__B3(B[2]), ._5__Vcc(1'b1), ._6__S2(S[1]), ._7__B2(B[1]),
    ._8__A2(A[1]), ._16__B4(B[3]), ._15__S4(S[3]), ._14__Cout(Cout), ._13__Cin(Cin), ._12__GND(1'b0),
    ._11__B1(B[0]), ._10__A1(A[0]), ._9__S1(S[0]));
endmodule
