// Logisim project ControlLib.circ as structural Verilog: 2 circuits, main circuit Control
// Ctrl
module Control (
  input  [15:0] Ins,
  output [10:0] control
);

  ROM #(.addrWidth(6), .dataWidth(11), .Select("low")) rom_1 (
    .addr({Ins[15:14], Ins[3:0]}), .data(control), .sel(1'b0));

  // Notes on the sheet:
  //   contents of rom_1 (hex, n*v repeats v):
  //   16 195 13 194 480 88 193 191 1d0 a0 11 190 12 480 192 10 16 195 13 194 480 288 193 191 1d0 a0 11 190
  //   12 480 192 10 16 195 13 194 480 80 193 191 1d0 a0 11 190 12 480 192 10 16 195 13 194 480 0 193 191
  //   1d0 a0 11 190 12 480 192 10
endmodule

module ControlDecoder (
  input  [10:0] in_1,
  output [2:0] AluOP,
  output Jump,
  output rWrite,
  output mWrite,
  output A_M,
  output R_I,
  output Dest,
  output JR,
  output Cjump
);


  assign A_M = in_1[6];
  assign AluOP = in_1[2:0];
  assign Cjump = in_1[10];
  assign Dest = in_1[8];
  assign JR = in_1[9];
  assign Jump = in_1[3];
  assign mWrite = in_1[5];
  assign R_I = in_1[7];
  assign rWrite = in_1[4];
endmodule
