// Logisim project ExecutionLib.circ as structural Verilog: 2 circuits, main circuit SignExtensionSelect
// SignEx
module SignExtensionSelect (
  input  [3:0] A,
  input  mWrite,
  input  mRead,
  output [7:0] O
);

  wire n7432_1__6__2y;

  _8Mux2X1 u_8mux2x1_1 (.E_prime(1'b0), .A({4'b0000, A}), .B({{5{A[3]}}, A[2:0]}), .S(n7432_1__6__2y), .out_5(O));
  _7432 u_7432_1 (
    ._4__2A(mWrite), ._5__2B(mRead), ._6__2Y(n7432_1__6__2y), ._7__GND(1'b0), ._14__Vcc(1'b1));  // open: _1__1A, _2__1B, _3__1Y, _13__4B, _12__4A, _11__4Y, _10__3B, _9__3A, _8__3Y
endmodule

// Ex
module Execution (
  input  [7:0] Data1,
  input  [7:0] Data2,
  input  [3:0] Imd,
  input  mWrite,
  input  mRead,
  input  R_I,
  input  [2:0] AluOp,
  output [7:0] Ans
);

  wire [7:0] n8mux2x1_1_out_5, signextensionselect_1_o;

  SignExtensionSelect signextensionselect_1 (.A(Imd), .O(signextensionselect_1_o), .mWrite(mWrite), .mRead(mRead));
  _8Mux2X1 u_8mux2x1_1 (.E_prime(1'b0), .A(Data2), .B(signextensionselect_1_o), .S(R_I), .out_5(n8mux2x1_1_out_5));
  // ALU alu_1: pin names not known; wires that end beside it: n8mux2x1_1_out_5, AluOp, Data1, Ans
endmodule
