// Logisim project InstructionFetchLib.circ as structural Verilog: 1 circuit, main circuit InstructionFetch
// IF
module InstructionFetch (
  input  [3:0] PrevSeg,
  input  [3:0] Offset,
  input  SegPreset,
  input  SegClr,
  input  PCPreset,
  input  PCClear,
  input  NoOp,
  input  clk,
  input  UJump,
  input  [7:0] UJumpAddress,
  output [3:0] segment,
  output [15:0] Instruction
);

  wire [3:2] n4mux2x1_2_o;
  wire [7:0] pcupdate_1_pc;
  wire [11:0] shifter_1_out;
  wire [15:0] rom_1_data;

  PCUpdate pcupdate_1 (
    .prev_segment(PrevSeg), .offset(Offset), .seg_preset(SegPreset), .seg_clr(SegClr), .pc_preset(PCPreset),
    .pc_clr(PCClear), .ujmp_address(UJumpAddress), .clk(clk), .ujmp_flag(UJump), .segment(segment),
    .pc(pcupdate_1_pc));
  Shifter #(.width(12), .shift("lr")) shifter_1 (.in({segment, pcupdate_1_pc}), .\dist (4'b0001), .out(shifter_1_out));
  ROM #(.addrWidth(12), .dataWidth(16), .Select("low")) rom_1 (
    .addr(shifter_1_out), .data({rom_1_data[15:14], Instruction[13:4], rom_1_data[3:0]}), .sel(1'b0));
  _4Mux2X1 u_4mux2x1_1 (.E_prime(1'b0), .A(rom_1_data[3:0]), .B(4'b0101), .S(NoOp), .O(Instruction[3:0]));
  _4Mux2X1 u_4mux2x1_2 (
    .E_prime(1'b0), .A({2'b00, rom_1_data[15:14]}), .B(4'b0010), .S(NoOp),
    .O({n4mux2x1_2_o, Instruction[15:14]}));
endmodule
