// Logisim project Memory.circ as structural Verilog: 1 circuit, main circuit main
module main (
  input  in_1,
  input  memRead,
  input  [7:0] Address__res,
  input  [7:0] WriteData__Data1,
  input  memWrite,
  input  nRAMEnable,
  input  Clear,
  output [7:0] val,
  output [7:0] ReadData
);

  wire clock_1_out;

  Clock clock_1 (.out(clock_1_out));
  RAM #(.bus("separate"), .simpleMode("false"), .Select("low")) ram_1 (
    .addr(Address__res), .din(WriteData__Data1), .data(ReadData), .str(memWrite), .sel(nRAMEnable),
    .clk(clock_1_out), .clr(Clear));  // open: ld
  _8Mux2X1 u_8mux2x1_1 (.E_prime(in_1), .A(Address__res), .B(ReadData), .S(memRead), .out_5(val));
endmodule
