// Logisim project MuxLib.circ as structural Verilog: 6 circuits, main circuit 32Mux2X1
// 32M2
module _32Mux2X1 (
  input  [31:0] A,
  input  [31:0] B,
  input  S,
  input  E_prime,
  output [31:0] O
);

  _4Mux2X1 u_4mux2x1_1 (.E_prime(E_prime), .A(A[15:12]), .B(B[15:12]), .S(S), .O(O[15:12]));
  _4Mux2X1 u_4mux2x1_2 (.E_prime(E_prime), .A(A[23:20]), .B(B[23:20]), .S(S), .O(O[23:20]));
  _4Mux2X1 u_4mux2x1_3 (.E_prime(E_prime), .A(A[31:28]), .B(B[31:28]), .S(S), .O(O[31:28]));
  _4Mux2X1 u_4mux2x1_4 (.E_prime(E_prime), .A(A[7:4]), .B(B[7:4]), .S(S), .O(O[7:4]));
  _4Mux2X1 u_4mux2x1_5 (.E_prime(E_prime), .A(A[3:0]), .B(B[3:0]), .S(S), .O(O[3:0]));
  _4Mux2X1 u_4mux2x1_6 (.E_prime(E_prime), .A(A[11:8]), .B(B[11:8]), .S(S), .O(O[11:8]));
  _4Mux2X1 u_4mux2x1_7 (.E_prime(E_prime), .A(A[19:16]), .B(B[19:16]), .S(S), .O(O[19:16]));
  _4Mux2X1 u_4mux2x1_8 (.E_prime(E_prime), .A(A[27:24]), .B(B[27:24]), .S(S), .O(O[27:24]));
endmodule

// 4M2
module _4Mux2X1 (
  input  E_prime,
  input  [3:0] A,
  input  [3:0] B,
  input  S,
  output [3:0] O
);

  _74157 u_74157_1 (
    ._1__S(S), ._2__A1(A[0]), ._3__B1(B[0]), ._4__Y1(O[0]), ._5__A2(A[1]), ._6__B2(B[1]), ._7__Y2(O[1]),
    ._8__GND(1'b0), ._16__Vcc(1'b1), ._15__G(E_prime), ._14__A4(A[2]), ._13__B4(B[2]), ._12__Y4(O[2]),
    ._11__A3(A[3]), ._10__B3(B[3]), ._9__Y3(O[3]));
endmodule

// 32M4
module _32Mux4X1 (
  input  [31:0] A,
  input  [31:0] B,
  input  [31:0] C,
  input  [31:0] D,
  input  E_prime,
  input  S1,
  input  S0,
  output [31:0] O
);

  wire [31:0] n32mux2x1_1_o, n32mux2x1_2_o;

  _32Mux2X1 u_32mux2x1_1 (.A(A), .B(B), .E_prime(E_prime), .S(S0), .O(n32mux2x1_1_o));
  _32Mux2X1 u_32mux2x1_2 (.A(C), .B(D), .E_prime(E_prime), .S(S0), .O(n32mux2x1_2_o));
  _32Mux2X1 u_32mux2x1_3 (.A(n32mux2x1_1_o), .B(n32mux2x1_2_o), .E_prime(E_prime), .S(S1), .O(O));
endmodule

// 4M4
module _4Mux4X1 (
  input  [3:0] A,
  input  [3:0] B,
  input  [3:0] C,
  input  [3:0] D,
  input  E_prime,
  input  S1,
  input  S0,
  output [3:0] O
);

  wire [3:0] n4mux2x1_1_o, n4mux2x1_2_o;

  _4Mux2X1 u_4mux2x1_1 (.E_prime(E_prime), .A(A), .B(B), .S(S0), .O(n4mux2x1_1_o));
  _4Mux2X1 u_4mux2x1_2 (.E_prime(E_prime), .A(C), .B(D), .S(S0), .O(n4mux2x1_2_o));
  _4Mux2X1 u_4mux2x1_3 (.E_prime(E_prime), .A(n4mux2x1_1_o), .B(n4mux2x1_2_o), .S(S1), .O(O));
endmodule

// 12M2
module _12Mux2X1 (
  input  [11:0] A,
  input  [11:0] B,
  input  E_prime,
  input  S,
  output [11:0] O
);

  _4Mux2X1 u_4mux2x1_1 (.E_prime(E_prime), .A(A[3:0]), .B(B[3:0]), .S(S), .O(O[3:0]));
  _4Mux2X1 u_4mux2x1_2 (.E_prime(E_prime), .A(A[7:4]), .B(B[7:4]), .S(S), .O(O[7:4]));
  _4Mux2X1 u_4mux2x1_3 (.E_prime(E_prime), .A(A[11:8]), .B(B[11:8]), .S(S), .O(O[11:8]));
endmodule

// 8M2
module _8Mux2X1 (
  input  E_prime,
  input  [7:0] A,
  input  [7:0] B,
  input  S,
  output [7:0] out_5
);

  _4Mux2X1 u_4mux2x1_1 (.E_prime(E_prime), .A(A[3:0]), .B(B[3:0]), .S(S), .O(out_5[3:0]));
  _4Mux2X1 u_4mux2x1_2 (.E_prime(E_prime), .A(A[7:4]), .B(B[7:4]), .S(S), .O(out_5[7:4]));
endmodule
