// Logisim project PCUpdate.circ as structural Verilog: 3 circuits, main circuit PCUpdate
// PCUpd
module PCUpdate (
  input  [3:0] prev_segment,
  input  [3:0] offset,
  input  seg_preset,
  input  seg_clr,
  input  pc_preset,
  input  pc_clr,
  input  [7:0] ujmp_address,
  input  clk,
  input  ujmp_flag,
  output [3:0] segment,
  output [7:0] pc
);

  wire [3:0] adder4_1_s, n4mux2x1_1_o, segincrement_1_inc;
  wire [7:0] adder8_1_s, n8mux2x1_1_out_5, sign_extension_out;

  Register #(.width(4), .Select("high")) seg_reg (
    .D(n4mux2x1_1_o), .en(1'b1), .Q(segment), .clk(clk), .clr(seg_clr), .cs(1'b1), .preset(seg_preset));
  SignExt4X8 sign_extension (.in(offset), .out(sign_extension_out));
  Register #(.Select("high")) pc_reg (
    .D({n8mux2x1_1_out_5[6:0], 1'b0}), .en(1'b1), .Q(pc), .clk(clk), .clr(pc_clr), .cs(1'b1),
    .preset(pc_preset));
  SegIncrement segincrement_1 (.s(sign_extension_out[7]), .m(adder8_1_s[7]), .inc(segincrement_1_inc));
  Adder4 adder4_1 (.A(segment), .B(segincrement_1_inc), .Cin(1'b0), .S(adder4_1_s));  // open: Cout
  Adder8 adder8_1 (.A(sign_extension_out), .B({1'b0, pc[7:1]}), .Cin(1'b1), .S(adder8_1_s));  // open: Cout
  _4Mux2X1 u_4mux2x1_1 (.E_prime(1'b0), .A(adder4_1_s), .B(prev_segment), .S(ujmp_flag), .O(n4mux2x1_1_o));
  _8Mux2X1 u_8mux2x1_1 (.E_prime(1'b0), .A(adder8_1_s), .B(ujmp_address), .S(ujmp_flag), .out_5(n8mux2x1_1_out_5));
endmodule

// SE4X8
module SignExt4X8 (
  input  [3:0] in,
  output [7:0] out
);


  assign out = {{5{in[3]}}, in[2:0]};
endmodule

// SegInc
module SegIncrement (
  input  s,
  input  m,
  output [3:0] inc
);

  _7408 u_7408_1 (
    ._4__2A(s), ._5__2B(m), ._6__2Y(inc[3]), ._7__GND(1'b0), ._14__Vcc(1'b1));  // open: _1__1A, _2__1B, _3__1Y, _13__4B, _12__4A, _11__4Y, _10__3B, _9__3A, _8__3Y

  assign inc[2:0] = {{2{inc[3]}}, m};
endmodule
