// Logisim project PipelineRegister.circ as structural Verilog: 1 circuit, main circuit pr
// PR
module pr (
  input  [7:0] in_1,
  input  [7:0] in_2,
  input  [3:0] in_3,
  input  [3:0] in_4,
  input  [15:0] in_5,
  input  [10:0] in_6,
  input  clk,
  output [7:0] out_8,
  output [7:0] out_9,
  output [3:0] out_10,
  output [3:0] out_11,
  output [15:0] out_12,
  output [10:0] out_13
);

  Register #(.trigger("falling"), .Select("low")) register_1 (.D(in_1), .Q(out_8), .clk(clk));  // open: en, clr
  Register #(.trigger("falling"), .Select("low")) register_2 (.D(in_2), .Q(out_9), .clk(clk));  // open: en, clr
  Register #(.width(4), .trigger("falling"), .Select("low")) register_3 (
    .D(in_3), .Q(out_10), .clk(clk));  // open: en, clr
  Register #(.width(4), .trigger("falling"), .Select("low")) register_4 (
    .D(in_4), .Q(out_11), .clk(clk));  // open: en, clr
  Register #(.width(16), .trigger("falling"), .Select("low")) register_5 (
    .D(in_5), .Q(out_12), .clk(clk));  // open: en, clr
  Register #(.width(11), .trigger("falling"), .Select("low")) register_6 (
    .D(in_6), .Q(out_13), .clk(clk));  // open: en, clr
endmodule
